// Logisim project logisim-sound-examples.circ as structural Verilog: 4 circuits, main circuit buzzer_example
module buzzer_example (
  input  [13:0] frequency,
  input  enable_sound
);

  wire [6:0] volume_out;
  wire [7:0] duty_cycle_out;

  Slider #(.width(7)) volume (.out(volume_out));
  Slider duty_cycle (.out(duty_cycle_out));
  // Buzzer #(.waveform("Square")) buzzer_1: pin names not known; wires that end beside it: frequency, enable_sound, volume_out, duty_cycle_out

  // Notes on the sheet:
  //   How to use:
  //   1) Select hand tool.
  //   2) Set enable sound to 1.
  //   4) Increase duty cycle above zero.
  //   5) Increase volume above zero.
  //   Audible range: 20-20000 Hz
  //   A4: 440 Hz
  //   3) Set frequency to 440 (A4 note: 440 Hz).
  //   6) Try different waveform types in the buzzer properties or different frequencies and duty cycles.
endmodule

module buzzer_example_2 (
  input  enable_sound,
  output [13:0] out_2,
  output [13:0] frequency
);

  wire [6:0] volume_out;
  wire [7:0] duty_cycle_out, frequency_offset_out;

  Slider frequency_offset (.out(frequency_offset_out));
  assign out_2 = {{6{1'b0}}, frequency_offset_out};  // Bit_Extender bit_extender_1
  Slider #(.width(7)) volume (.out(volume_out));
  Slider duty_cycle (.out(duty_cycle_out));
  Adder #(.width(14)) adder_1 (.a(out_2), .b(14'h1b8), .out(frequency));  // open: cin, cout
  // Buzzer #(.waveform("Square")) buzzer_1: pin names not known; wires that end beside it: frequency, enable_sound, volume_out, duty_cycle_out

  // Notes on the sheet:
  //   Audible range: 20-20000 Hz
  //   A4: 440 Hz
  //   How to use:
  //   1) Select hand tool.
  //   2) Set enable sound to 1.
  //   4) Increase duty cycle above zero.
  //   5) Increase volume above zero.
  //   Same as buzzer_example, but here the frequency can be set by using a slider to add an offset to the 440 Hz frequency of the A4 note.
  //   3) Set frequency_offset to zero (which sets frequency to 440 Hz, i.e. the A4 note).
  //   6) Try different waveform types in the buzzer properties or different frequencies and duty cycles.
endmodule

module scale_example (
  input  enable_sound,
  output [13:0] C4,
  output [13:0] D4,
  output [13:0] E4,
  output [13:0] F4,
  output [13:0] G4,
  output [13:0] A4,
  output [13:0] B4,
  output [13:0] C5,
  output [13:0] frequency_current,
  output [2:0] counter
);

  wire CLK_out;
  wire [6:0] volume_out;
  wire [7:0] duty_cycle_out;

  Clock CLK (.out(CLK_out));
  countupdown countupdown_1 (.CLK(CLK_out), .CNT(counter));
  Multiplexer #(.select(3), .width(14)) multiplexer_1 (
    .in0(14'h106), .in1(14'h126), .in2(14'h14a), .in3(14'h15d), .in4(14'h188), .in5(14'h1b8), .in6(14'h1ee),
    .in7(14'h20b), .out(frequency_current), .sel(counter));
  Slider #(.width(7)) volume (.out(volume_out));
  Slider duty_cycle (.out(duty_cycle_out));
  // Buzzer buzzer_1: pin names not known; wires that end beside it: frequency_current, enable_sound, volume_out, duty_cycle_out

  assign A4 = 14'h1b8;
  assign B4 = 14'h1ee;
  assign C4 = 14'h106;
  assign C5 = 14'h20b;
  assign D4 = 14'h126;
  assign E4 = 14'h14a;
  assign F4 = 14'h15d;
  assign G4 = 14'h188;

  // Other names for the same wires on the sheet: f[13:0] = frequency_current

  // Notes on the sheet:
  //   How to use:
  //   1) Select hand tool.
  //   2) Set enable sound to 1.
  //   3) Increase volume above zero.
  //   Audible range: 20-20000 Hz
  //   A4: 440 Hz
  //   4) Enable auto-tick: Simulate->Auto-tick enabled.
endmodule

module countupdown (
  input  CLK,
  output [2:0] CNT
);

  wire counter_1_carry, d_ff_1_q, d_ff_1_qn;

  Counter #(.max('h7), .width(3)) counter_1 (
    .up(d_ff_1_q), .clk(CLK), .carry(counter_1_carry), .Q(CNT));  // open: clr, load, count, D
  // Probe on counter_1_carry
  D_Flip_Flop d_ff_1 (.D(d_ff_1_qn), .clk(counter_1_carry), .Q(d_ff_1_q), .Qn(d_ff_1_qn));  // open: preset, reset
  // Probe on d_ff_1_q

  // Notes on the sheet:
  //   Sub-circuit used in scale_example to count up from 0 to 7 and back down to 0.
endmodule
